# Fritzing sketch esquematico_eletrico_fritzing (saved by Fritzing 0.9.3b)

parts:
  Part1 = Arduino Mega 2560 (Rev3)
  hc-sr1 = hc-sr04
  Part2 = Motor Driver 1A Dual TB6612FNG
  A1 = AS5600 module
  Fonte_7V = 2.1mm Barrel Jack with Terminal Block
  M1 = DC Motor

nets:
  N1: Part1.D21/SCL, A1.Pin_6
  N2: Part1.D20/SDA, A1.Pin_4, A1.Pin_5
  GND: Part1.GND, hc-sr1.GND, A1.Pin_3
  N3: Part1.3V3, A1.Pin_1, A1.Pin_2
  VCC: Part1.5V, hc-sr1.VCC, Part2.VCC
  N4: Part1.D2_PWM, Part2.PWMA
  N5: Part1.D22, Part2.AIN1
  N6: Part1.D23, Part2.AIN2
  N7: Part1.D24, Part2.STBY
  N8: Part1.D51, hc-sr1.Echo
  N9: Part1.D53, hc-sr1.Trig
  N10: Part2.GND, Fonte_7V.POS
  N11: Part2.A02, M1.pin_1
  N12: Part2.A01, M1.pin_2
  N13: Part2.VM, Fonte_7V.NEG

notes:
  Fonte 7V DC
  Motor DC
  Ponte H
  Sensor Hall
  Arduino Mega 2650
  Sensor Ultrassônico

custom parts:
  AS5600 module: .This module is mainly placed behind the stepper motor to obtain the rotation angle of the stepper motor.
